# Fritzing sketch Zenith80 (saved by Fritzing 0.9.3b)
breadboards: 1
perfboards: 2

parts:
  CPU = Z80 A [package="DIP (Dual Inline) [THT]"]
  Battery = Lithium Ion Polymer Battery 3.7v 1200mAh [part_number=258]
  PowerBoost = PowerBoost 500 Charger
  MMU = LQFP-32 [chip_label=MMU package=LQFP]

nets:
  A11: CPU.A11, MMU.17
  A12: CPU.A12, MMU.16
  A13: CPU.A13, MMU.15
  A14: CPU.A14, MMU.14
  A15: CPU.A15, MMU.13
  CPU_CLK: CPU.CLK
  D4: CPU.D4
  D3: CPU.D3
  D5: CPU.D5
  D6: CPU.D6
  5V: CPU.+5V, PowerBoost.5.0V, MMU.1
  D2: CPU.D2
  D7: CPU.D7
  D0: CPU.D0
  D1: CPU.D1
  GND: CPU.GND, Battery.negative, PowerBoost.GND, MMU.32
  A0: CPU.A0, MMU.2
  A1: CPU.A1, MMU.3
  A2: CPU.A2, MMU.4
  A3: CPU.A3, MMU.5
  A4: CPU.A4, MMU.6
  A5: CPU.A5, MMU.7
  A6: CPU.A6, MMU.8
  A7: CPU.A7, MMU.9
  A8: CPU.A8, MMU.10
  A9: CPU.A9, MMU.11
  A10: CPU.A10, MMU.12
  N1: Battery.positive, PowerBoost.VBAT

custom parts:
  Z80 A: Zilog Z80 A CPU
  Lithium Ion Polymer Battery 3.7v 1200mAh: Lithium ion polymer (also known as 'lipo' or 'lipoly') batteries are thin, light and powerful. The output ranges from 4.2V when completely charged to 3.7V. This battery has a capacity of 1200mAh for a total of about 4.5 Wh. The batteries come pre-attached with a genuine 2-pin JST-PH connector as shown and include the necessary protection circuitry.
  PowerBoost 500 Charger: The PowerBoost 500C is a little DC/DC boost converter module that can be powered by any 3.7V LiIon/LiPoly battery, and convert the battery output to 5.2V DC for running your 5V projects. At its heart is a TPS61090 boost converter from TI. This boost converter chip has some really nice extras such as low battery detection, 2A internal switch, synchronous conversion, excellent efficiency, and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
